# Fritzing sketch Extension (saved by Fritzing 0.9.4)
breadboards: 1

parts:
  Part1 = Arduino Nano (Rev3.0)
  Part2 = Arduino Nano (Rev3.0)
  Part3 = Arduino Nano (Rev3.0)

nets:
  GND: Part1.GND, Part2.GND, Part3.GND
  VIN: Part1.5V, Part2.VIN, Part3.VIN
  N1: Part1.A5, Part2.A5, Part3.A5
  N2: Part1.A4, Part2.A4, Part3.A4

notes:
  MASTER
  SLAVE 1 (address 5)
  SLAVE 2 (address 6)
